// Digital circuit computer.dig as structural Verilog
module computer (
  input  clk,
  input  in_3,
  output [15:0] A
);

  wire C, halt_15, ld_12, str_11;
  wire [1:0] sel_a_2_3, sel_alu_0_1, sel_b_4_5;
  wire [3:0] counter_1_out;
  wire [14:6] Instruction_d;
  wire [15:0] Arithmath_s, Data_d, multiplexer_1_out, multiplexer_2_out;

  Counter #(.Bits(4)) counter_1 (.en(in_3), .C(C), .clr(1'b0), .out(counter_1_out));  // open: ovf
  and and_1 (C, clk, halt_15);
  EEPROMDualPort #(.AddrBits(4), .Bits(16)) Data (
    .A(counter_1_out), .Din(A), .str(str_11), .C(C), .ld(ld_12), .D(Data_d));
  EEPROMDualPort #(.AddrBits(4), .Bits(16)) Instruction (
    .A(counter_1_out), .Din({16{1'b0}}), .str(1'b0), .C(C), .ld(1'b1),
    .D({halt_15, Instruction_d[14:13], ld_12, str_11, Instruction_d[10:6], sel_b_4_5, sel_a_2_3, sel_alu_0_1}));
  Multiplexer #(.Selector_Bits(2), .Bits(16)) multiplexer_1 (
    .sel(sel_b_4_5), .in_0(Data_d), .in_1({16{1'b0}}), .in_2({16{1'b0}}), .in_3({16{1'b0}}),
    .out(multiplexer_1_out));
  _16bits_alu Arithmath (
    .A(multiplexer_2_out), .B(multiplexer_1_out), .Sel(sel_alu_0_1), .S(Arithmath_s));  // open: C_out, ZF
  Register #(.Bits(16)) register_1 (.D(Arithmath_s), .C(C), .en(in_3), .Q(A));
  Multiplexer #(.Selector_Bits(2), .Bits(16)) multiplexer_2 (
    .sel(sel_a_2_3), .in_0(A), .in_1({16{1'b0}}), .in_2({16{1'b0}}), .in_3({16{1'b0}}),
    .out(multiplexer_2_out));

  // Other names for the same wires on the sheet: Clock = clk; Enable = in_3

  // Notes on the sheet:
  //   contents of Data (hex, n*v repeats v):
  //   a,14,1e,28,14,a,a,a
  //   contents of Instruction (hex, n*v repeats v):
  //   9000,9000,9000,9001,8814,9000,9000
endmodule
